// Logisim project SamSmithLogisim.circ as structural Verilog
module My_DLatch (
  input  C,
  input  D,
  output Q,
  output Q_invert
);

  wire and_1_out, and_2_out, not_1_out, or_1_out, or_2_out;

  not not_1 (not_1_out, D);
  and and_1 (and_1_out, C, not_1_out);
  and and_2 (and_2_out, C, D);
  or or_1 (or_1_out, and_1_out, Q_invert);
  or or_2 (or_2_out, Q, and_2_out);
  not not_2 (Q, or_1_out);
  not not_3 (Q_invert, or_2_out);
endmodule

module My_SRLatch (
  input  R,
  input  S,
  output Q,
  output Q_invert
);

  wire or_1_out, or_2_out;

  or or_1 (or_1_out, R, Q_invert);
  or or_2 (or_2_out, Q, S);
  not not_1 (Q, or_1_out);
  not not_2 (Q_invert, or_2_out);
endmodule

module My_D_FlipFlop (
  input  C,
  input  D,
  output out_3
);

  wire my_dlatch_1_q, not_1_out;

  My_DLatch my_dlatch_1 (.C(C), .D(D), .Q(my_dlatch_1_q));  // open: Q_invert
  not not_1 (not_1_out, C);
  My_DLatch my_dlatch_2 (.C(not_1_out), .D(my_dlatch_1_q), .Q(out_3));  // open: Q_invert
endmodule

module My_Register (
  input  C,
  input  [7:0] in_2,
  output [7:0] out_3
);

  D_Flip_Flop #(.trigger("falling")) d_ff_1 (.D(in_2[0]), .clk(C), .Q(out_3[0]));  // open: Qn, preset, reset
  D_Flip_Flop #(.trigger("falling")) d_ff_2 (.D(in_2[1]), .clk(C), .Q(out_3[1]));  // open: Qn, preset, reset
  D_Flip_Flop #(.trigger("falling")) d_ff_3 (.D(in_2[2]), .clk(C), .Q(out_3[2]));  // open: Qn, preset, reset
  D_Flip_Flop #(.trigger("falling")) d_ff_4 (.D(in_2[3]), .clk(C), .Q(out_3[3]));  // open: Qn, preset, reset
  D_Flip_Flop #(.trigger("falling")) d_ff_5 (.D(in_2[4]), .clk(C), .Q(out_3[4]));  // open: Qn, preset, reset
  D_Flip_Flop #(.trigger("falling")) d_ff_6 (.D(in_2[5]), .clk(C), .Q(out_3[5]));  // open: Qn, preset, reset
  D_Flip_Flop #(.trigger("falling")) d_ff_7 (.D(in_2[6]), .clk(C), .Q(out_3[6]));  // open: Qn, preset, reset
  D_Flip_Flop #(.trigger("falling")) d_ff_8 (.D(in_2[7]), .clk(C), .Q(out_3[7]));  // open: Qn, preset, reset
endmodule

module My_Register_File (
  input  [7:0] Data,
  input  Clock,
  input  write_en,
  input  [2:0] reg_w_sel,
  input  [2:0] reg_ra_sel,
  input  [2:0] reg_rb_sel,
  output [7:0] regA,
  output [7:0] regB
);

  wire demultiplexer_1_out1, demultiplexer_1_out2, demultiplexer_1_out3, demultiplexer_1_out4,
       demultiplexer_1_out5, demultiplexer_1_out6, demultiplexer_1_out7;
  wire [7:0] register_1_q, register_2_q, register_3_q, register_4_q, register_5_q, register_6_q, register_7_q;

  Demultiplexer #(.select(3)) demultiplexer_1 (
    .out1(demultiplexer_1_out1), .out2(demultiplexer_1_out2), .out3(demultiplexer_1_out3),
    .out4(demultiplexer_1_out4), .out5(demultiplexer_1_out5), .out6(demultiplexer_1_out6),
    .out7(demultiplexer_1_out7), .in(write_en), .sel(reg_w_sel));  // open: out0
  Register #(.trigger("falling")) register_1 (
    .D(Data), .en(demultiplexer_1_out1), .clk(Clock), .Q(register_1_q));  // open: clr
  Register #(.trigger("falling")) register_2 (
    .D(Data), .en(demultiplexer_1_out2), .clk(Clock), .Q(register_2_q));  // open: clr
  Register #(.trigger("falling")) register_3 (
    .D(Data), .en(demultiplexer_1_out3), .clk(Clock), .Q(register_3_q));  // open: clr
  Register #(.trigger("falling")) register_4 (
    .D(Data), .en(demultiplexer_1_out4), .clk(Clock), .Q(register_4_q));  // open: clr
  Register #(.trigger("falling")) register_5 (
    .D(Data), .en(demultiplexer_1_out5), .clk(Clock), .Q(register_5_q));  // open: clr
  Register #(.trigger("falling")) register_6 (
    .D(Data), .en(demultiplexer_1_out6), .clk(Clock), .Q(register_6_q));  // open: clr
  Register #(.trigger("falling")) register_7 (
    .D(Data), .en(demultiplexer_1_out7), .clk(Clock), .Q(register_7_q));  // open: clr
  Multiplexer #(.select(3), .width(8)) multiplexer_1 (
    .in0({8{1'b0}}), .in1(register_1_q), .in2(register_2_q), .in3(register_3_q), .in4(register_4_q),
    .in5(register_5_q), .in6(register_6_q), .in7(register_7_q), .out(regA), .sel(reg_ra_sel));
  Multiplexer #(.select(3), .width(8)) multiplexer_2 (
    .in0({8{1'b0}}), .in1(register_1_q), .in2(register_2_q), .in3(register_3_q), .in4(register_4_q),
    .in5(register_5_q), .in6(register_6_q), .in7(register_7_q), .out(regB), .sel(reg_rb_sel));
endmodule

module My_Binary_Decoder (
  input  [1:0] in_1
);

  wire and_1_out, and_2_out, and_3_out, and_4_out, not_1_out, not_2_out, not_3_out, not_4_out;

  not not_1 (not_1_out, in_1[0]);
  not not_2 (not_2_out, in_1[1]);
  not not_3 (not_3_out, in_1[0]);
  not not_4 (not_4_out, in_1[1]);
  and and_1 (and_1_out, in_1[0], in_1[1]);
  LED Three (.in(and_1_out));
  and and_2 (and_2_out, not_1_out, in_1[1]);
  LED Two (.in(and_2_out));
  and and_3 (and_3_out, in_1[0], not_2_out);
  LED One (.in(and_3_out));
  and and_4 (and_4_out, not_3_out, not_4_out);
  LED Zero (.in(and_4_out));
endmodule

module My_Not (
  input  in_1,
  output out_2
);

  Transistor transistor_1 (.in(1'b1), .out(out_2), .gate(in_1));
  Transistor #(.\type ("n")) transistor_2 (.in(1'b0), .out(out_2), .gate(in_1));
endmodule

module My_And (
  input  in_1,
  input  in_2,
  output out_3
);

  wire transistor_1_out, transistor_3_out;

  Transistor transistor_1 (.in(1'b1), .out(transistor_1_out), .gate(in_2));
  Transistor #(.\type ("n")) transistor_2 (.in(transistor_3_out), .out(transistor_1_out), .gate(in_1));
  Transistor #(.\type ("n")) transistor_3 (.in(1'b0), .out(transistor_3_out), .gate(in_2));
  Transistor transistor_4 (.in(1'b1), .out(transistor_1_out), .gate(in_1));
  not not_1 (out_3, transistor_1_out);
endmodule

module My_Nand (
  input  in_1,
  input  in_2,
  output out_3
);

  wire transistor_3_out;

  Transistor transistor_1 (.in(1'b1), .out(out_3), .gate(in_2));
  Transistor #(.\type ("n")) transistor_2 (.in(transistor_3_out), .out(out_3), .gate(in_1));
  Transistor #(.\type ("n")) transistor_3 (.in(1'b0), .out(transistor_3_out), .gate(in_2));
  Transistor transistor_4 (.in(1'b1), .out(out_3), .gate(in_1));
endmodule

module My_Nor (
  input  in_1,
  input  in_2,
  output out_3
);

  wire nand_1_out, nand_2_out, nand_3_out;

  nand nand_1 (nand_1_out, in_1, in_1);
  nand nand_2 (nand_2_out, in_2, in_2);
  nand nand_3 (nand_3_out, nand_1_out, nand_2_out);
  // NAND_Gate nand_4 has open pins: out=out_3
endmodule

module My_Or (
  input  in_1,
  input  in_2,
  output out_3
);

  wire nand_1_out, nand_2_out;

  nand nand_1 (nand_1_out, in_1, in_1);
  nand nand_2 (nand_2_out, in_2, in_2);
  nand nand_3 (out_3, nand_1_out, nand_2_out);
endmodule

module My_Multiplexer (
  input  [7:0] A_00,
  input  [7:0] B_01,
  input  [7:0] C_10,
  input  [7:0] D_11,
  input  [1:0] SEL,
  output [7:0] out_6
);

  wire not_1_out, not_2_out, not_3_out, not_4_out;
  wire [7:0] and_1_out, and_2_out, and_3_out, and_4_out, and_5_out, and_6_out, and_7_out, and_8_out,
       bit_extender_1_out, bit_extender_2_out, bit_extender_3_out, bit_extender_4_out, bit_extender_5_out,
       bit_extender_6_out, bit_extender_7_out, bit_extender_8_out;

  assign bit_extender_1_out = {{7{not_1_out}}, not_1_out};  // Bit_Extender bit_extender_1
  not not_1 (not_1_out, SEL[1]);
  not not_2 (not_2_out, SEL[0]);
  assign bit_extender_2_out = {{7{not_2_out}}, not_2_out};  // Bit_Extender bit_extender_2
  assign bit_extender_3_out = {{7{not_3_out}}, not_3_out};  // Bit_Extender bit_extender_3
  not not_3 (not_3_out, SEL[1]);
  assign bit_extender_4_out = {{7{SEL[0]}}, SEL[0]};  // Bit_Extender bit_extender_4
  assign bit_extender_5_out = {{7{SEL[1]}}, SEL[1]};  // Bit_Extender bit_extender_5
  not not_4 (not_4_out, SEL[0]);
  assign bit_extender_6_out = {{7{not_4_out}}, not_4_out};  // Bit_Extender bit_extender_6
  assign bit_extender_7_out = {{7{SEL[1]}}, SEL[1]};  // Bit_Extender bit_extender_7
  assign bit_extender_8_out = {{7{SEL[0]}}, SEL[0]};  // Bit_Extender bit_extender_8
  assign and_1_out = bit_extender_1_out & bit_extender_2_out;  // AND_Gate and_1, 8 bits wide
  assign and_2_out = bit_extender_3_out & bit_extender_4_out;  // AND_Gate and_2, 8 bits wide
  assign and_3_out = bit_extender_5_out & bit_extender_6_out;  // AND_Gate and_3, 8 bits wide
  assign and_4_out = bit_extender_7_out & bit_extender_8_out;  // AND_Gate and_4, 8 bits wide
  assign and_5_out = A_00 & and_1_out;  // AND_Gate and_5, 8 bits wide
  assign and_6_out = B_01 & and_2_out;  // AND_Gate and_6, 8 bits wide
  assign and_7_out = C_10 & and_3_out;  // AND_Gate and_7, 8 bits wide
  assign and_8_out = D_11 & and_4_out;  // AND_Gate and_8, 8 bits wide
  assign out_6 = and_5_out | and_6_out | and_7_out | and_8_out;  // OR_Gate or_1, 8 bits wide
endmodule

module My_Demultiplexer (
  input  [7:0] in_1,
  input  [1:0] SEL,
  output [7:0] A,
  output [7:0] B,
  output [7:0] C,
  output [7:0] D
);

  wire [7:0] and_1_out, and_2_out, and_3_out, and_4_out, bit_extender_1_out, bit_extender_2_out, not_1_out,
       not_2_out, not_3_out, not_4_out;

  assign bit_extender_1_out = {{7{SEL[0]}}, SEL[0]};  // Bit_Extender bit_extender_1
  assign bit_extender_2_out = {{7{SEL[1]}}, SEL[1]};  // Bit_Extender bit_extender_2
  assign not_1_out = ~bit_extender_1_out;  // NOT_Gate not_1, 8 bits wide
  assign not_2_out = ~bit_extender_2_out;  // NOT_Gate not_2, 8 bits wide
  assign not_3_out = ~bit_extender_2_out;  // NOT_Gate not_3, 8 bits wide
  assign not_4_out = ~bit_extender_1_out;  // NOT_Gate not_4, 8 bits wide
  assign and_1_out = not_1_out & not_2_out;  // AND_Gate and_1, 8 bits wide
  assign and_2_out = bit_extender_1_out & not_3_out;  // AND_Gate and_2, 8 bits wide
  assign and_3_out = not_4_out & bit_extender_2_out;  // AND_Gate and_3, 8 bits wide
  assign and_4_out = bit_extender_1_out & bit_extender_2_out;  // AND_Gate and_4, 8 bits wide
  assign A = in_1 & and_1_out;  // AND_Gate and_5, 8 bits wide
  assign B = in_1 & and_2_out;  // AND_Gate and_6, 8 bits wide
  assign C = in_1 & and_3_out;  // AND_Gate and_7, 8 bits wide
  assign D = in_1 & and_4_out;  // AND_Gate and_8, 8 bits wide
endmodule

module My_SignExtender (
  input  in_1,
  output [7:0] out_2
);

  and and_1 (out_2[0], 1'b1, in_1);
  and and_2 (out_2[1], 1'b1, in_1);
  and and_3 (out_2[2], 1'b1, in_1);
  and and_4 (out_2[3], 1'b1, in_1);
  and and_5 (out_2[4], 1'b1, in_1);
  and and_6 (out_2[5], 1'b1, in_1);
  and and_7 (out_2[6], 1'b1, in_1);
  and and_8 (out_2[7], 1'b1, in_1);
endmodule

module My_OneBitAdder (
  input  a,
  input  b,
  input  c_in,
  output res,
  output c_out
);

  wire and_1_out, and_2_out, xor_1_out;

  xor xor_1 (xor_1_out, a, b);
  and and_1 (and_1_out, xor_1_out, c_in);
  and and_2 (and_2_out, a, b);
  xor xor_2 (res, xor_1_out, c_in);
  or or_1 (c_out, and_1_out, and_2_out);
endmodule

module My_CarryRippleAdder (
  input  [3:0] a,
  input  [3:0] b,
  output [3:0] out_3
);

  wire my_onebitadder_1_c_out, my_onebitadder_2_c_out, my_onebitadder_3_c_out, undriven;

  My_OneBitAdder my_onebitadder_1 (.a(a[0]), .b(b[0]), .c_in(undriven), .res(out_3[0]), .c_out(my_onebitadder_1_c_out));
  My_OneBitAdder my_onebitadder_2 (
    .a(a[1]), .b(b[1]), .c_in(my_onebitadder_1_c_out), .res(out_3[1]), .c_out(my_onebitadder_2_c_out));
  My_OneBitAdder my_onebitadder_3 (
    .a(a[2]), .b(b[2]), .c_in(my_onebitadder_2_c_out), .res(out_3[2]), .c_out(my_onebitadder_3_c_out));
  My_OneBitAdder my_onebitadder_4 (.a(a[3]), .b(b[3]), .c_in(my_onebitadder_3_c_out), .c_out(out_3[3]));  // open: res
endmodule

module ALU_Basic (
  input  A,
  input  A_inv,
  input  less,
  input  B,
  input  B_inv,
  input  C_in,
  input  [1:0] func,
  output result,
  output c_out
);

  wire and_1_out, multiplexer_1_out, multiplexer_2_out, my_onebitadder_1_res, not_1_out, not_2_out, or_1_out;

  not not_1 (not_1_out, A);
  not not_2 (not_2_out, B);
  Multiplexer multiplexer_1 (.in0(A), .in1(not_1_out), .out(multiplexer_1_out), .sel(A_inv));
  Multiplexer multiplexer_2 (.in0(B), .in1(not_2_out), .out(multiplexer_2_out), .sel(B_inv));
  and and_1 (and_1_out, multiplexer_1_out, multiplexer_2_out);
  or or_1 (or_1_out, multiplexer_1_out, multiplexer_2_out);
  My_OneBitAdder my_onebitadder_1 (
    .a(multiplexer_1_out), .b(multiplexer_2_out), .c_in(C_in), .res(my_onebitadder_1_res), .c_out(c_out));
  Multiplexer #(.select(2)) multiplexer_3 (
    .in0(and_1_out), .in1(or_1_out), .in2(my_onebitadder_1_res), .in3(less), .out(result), .sel(func));
endmodule

module My_MSB_ALU (
  input  A,
  input  A_inv,
  input  less,
  input  B,
  input  B_inv,
  input  C_in,
  input  [1:0] func,
  output result,
  output slt,
  output overflow
);

  wire and_1_out, multiplexer_1_out, multiplexer_2_out, my_onebitadder_1_c_out, not_1_out, not_2_out,
       or_1_out;

  not not_1 (not_1_out, A);
  not not_2 (not_2_out, B);
  Multiplexer multiplexer_1 (.in0(A), .in1(not_1_out), .out(multiplexer_1_out), .sel(A_inv));
  Multiplexer multiplexer_2 (.in0(B), .in1(not_2_out), .out(multiplexer_2_out), .sel(B_inv));
  and and_1 (and_1_out, multiplexer_1_out, multiplexer_2_out);
  or or_1 (or_1_out, multiplexer_1_out, multiplexer_2_out);
  My_OneBitAdder my_onebitadder_1 (
    .a(multiplexer_1_out), .b(multiplexer_2_out), .c_in(C_in), .res(slt), .c_out(my_onebitadder_1_c_out));
  Multiplexer #(.select(2)) multiplexer_3 (
    .in0(and_1_out), .in1(or_1_out), .in2(slt), .in3(less), .out(result), .sel(func));
  xor xor_1 (overflow, my_onebitadder_1_c_out, C_in);
endmodule

module My_8Bit_ALU (
  input  [3:0] opcode,
  input  [7:0] A,
  input  [7:0] B,
  output is_zero,
  output [7:0] main_output,
  output overflow
);

  wire alu_basic_1_c_out, alu_basic_2_c_out, alu_basic_3_c_out, alu_basic_4_c_out, alu_basic_5_c_out,
       alu_basic_6_c_out, alu_basic_7_c_out, my_msb_alu_1_slt, or_1_out;

  ALU_Basic alu_basic_1 (
    .A(A[0]), .A_inv(opcode[3]), .B(B[0]), .B_inv(opcode[2]), .C_in(opcode[2]), .func(opcode[1:0]),
    .less(my_msb_alu_1_slt), .c_out(alu_basic_1_c_out), .result(main_output[0]));
  ALU_Basic alu_basic_2 (
    .A(A[1]), .A_inv(opcode[3]), .B(B[1]), .B_inv(opcode[2]), .C_in(alu_basic_1_c_out), .func(opcode[1:0]),
    .less(1'b0), .c_out(alu_basic_2_c_out), .result(main_output[1]));
  ALU_Basic alu_basic_3 (
    .A(A[2]), .A_inv(opcode[3]), .B(B[2]), .B_inv(opcode[2]), .C_in(alu_basic_2_c_out), .func(opcode[1:0]),
    .less(1'b0), .c_out(alu_basic_3_c_out), .result(main_output[2]));
  ALU_Basic alu_basic_4 (
    .A(A[3]), .A_inv(opcode[3]), .B(B[3]), .B_inv(opcode[2]), .C_in(alu_basic_3_c_out), .func(opcode[1:0]),
    .less(1'b0), .c_out(alu_basic_4_c_out), .result(main_output[3]));
  ALU_Basic alu_basic_5 (
    .A(A[4]), .A_inv(opcode[3]), .B(B[4]), .B_inv(opcode[2]), .C_in(alu_basic_4_c_out), .func(opcode[1:0]),
    .less(1'b0), .c_out(alu_basic_5_c_out), .result(main_output[4]));
  ALU_Basic alu_basic_6 (
    .A(A[5]), .A_inv(opcode[3]), .B(B[5]), .B_inv(opcode[2]), .C_in(alu_basic_5_c_out), .func(opcode[1:0]),
    .less(1'b0), .c_out(alu_basic_6_c_out), .result(main_output[5]));
  ALU_Basic alu_basic_7 (
    .A(A[6]), .A_inv(opcode[3]), .B(B[6]), .B_inv(opcode[2]), .C_in(alu_basic_6_c_out), .func(opcode[1:0]),
    .less(1'b0), .c_out(alu_basic_7_c_out), .result(main_output[6]));
  My_MSB_ALU my_msb_alu_1 (
    .A(A[7]), .A_inv(opcode[3]), .B(B[7]), .B_inv(opcode[2]), .func(opcode[1:0]), .C_in(alu_basic_7_c_out),
    .less(1'b0), .result(main_output[7]), .slt(my_msb_alu_1_slt), .overflow(overflow));
  or or_1 (or_1_out, main_output[0], main_output[1], main_output[2], main_output[3], main_output[4], main_output[5], main_output[6], main_output[7]);
  not not_1 (is_zero, or_1_out);
endmodule

module testing (
  input  [3:0] op_code,
  input  [7:0] A,
  input  [7:0] B
);

  wire my_8bit_alu_1_overflow;
  wire [7:0] my_8bit_alu_1_main_output;

  My_8Bit_ALU my_8bit_alu_1 (
    .A(A), .B(B), .opcode(op_code), .main_output(my_8bit_alu_1_main_output), .overflow(my_8bit_alu_1_overflow));  // open: is_zero
  LED led_1 ();  // open: in
  Register register_1 (.D(my_8bit_alu_1_main_output));  // open: en, clk, Q, clr
endmodule

module review (
  input  in_1,
  output out_2
);

  Transistor transistor_1 (.in(1'b1), .out(out_2), .gate(in_1));
  Transistor #(.\type ("n")) transistor_2 (.in(1'b0), .out(out_2), .gate(in_1));
endmodule

module r (
  input  in_1,
  input  in_2,
  input  in_3,
  input  [7:0] in_4,
  input  in_5,
  input  [1:0] in_6,
  input  in_7,
  input  [3:0] in_8,
  input  [7:0] in_9,
  input  [7:0] in_10,
  input  [7:0] in_11,
  input  [7:0] in_12,
  input  [1:0] in_13,
  input  [2:0] a_sel,
  input  [7:0] data,
  input  [2:0] w_sel,
  input  [2:0] b_sel,
  input  w_en,
  output out_19,
  output out_20,
  output [7:0] out_21,
  output [7:0] out_22,
  output out_23,
  output [7:0] out_24,
  output [7:0] out_25,
  output out_26,
  output [7:0] out_27,
  output [7:0] A,
  output [7:0] B
);

  wire clock_1_out, review_1_out_2, transistor_3_out;

  LED led_1 (.in(in_8[3]));
  LED led_2 (.in(in_8[2]));
  review review_1 (.in_1(in_2), .out_2(review_1_out_2));
  review review_2 (.in_1(in_3), .out_2(out_23));
  review review_3 (.in_1(in_3), .out_2(out_23));
  LED led_3 (.in(in_8[1]));
  LED led_4 (.in(in_8[0]));
  Multiplexer #(.select(2), .width(8)) multiplexer_1 (
    .in0(in_9), .in1(in_10), .in2(in_11), .in3(in_12), .out(out_27), .sel(in_13));
  review review_4 (.in_1(review_1_out_2), .out_2(out_20));
  My_Not my_not_1 (.in_1(in_1), .out_2(out_19));
  Transistor transistor_1 (.in(1'b1), .out(out_26), .gate(in_7));
  Transistor #(.\type ("n")) transistor_2 (.in(transistor_3_out), .out(out_26), .gate(in_5));
  Transistor #(.\type ("n")) transistor_3 (.in(1'b0), .out(transistor_3_out), .gate(in_7));
  My_Not my_not_2 (.in_1(in_1), .out_2(out_19));
  Transistor transistor_4 (.in(1'b1), .out(out_26), .gate(in_5));
  Clock clock_1 (.out(clock_1_out));
  My_Register_File my_register_file_1 (
    .Clock(clock_1_out), .write_en(w_en), .reg_ra_sel(a_sel), .reg_rb_sel(b_sel), .reg_w_sel(w_sel),
    .Data(data), .regA(A), .regB(B));
  My_Demultiplexer my_demultiplexer_1 (.SEL(in_6), .in_1(in_4), .A(out_21), .B(out_22), .C(out_24), .D(out_25));
endmodule

module PNP_transistor (
  input  in_1,
  output out_2
);

  Transistor transistor_1 (.in(1'b1), .out(out_2), .gate(in_1));
endmodule

module NPN_transistor (
  input  in_1,
  output out_2
);

  Transistor #(.\type ("n")) transistor_1 (.in(1'b0), .out(out_2), .gate(in_1));
endmodule

module My_CPU (
);

  wire BNE, clock_tunnel, Jump, multiplexer_3_out, multiplexer_4_out, my_8bit_alu_1_is_zero,
       my_8bit_alu_1_overflow, my_8bit_alu_2_is_zero, my_8bit_alu_2_overflow, my_control_1_go_to_ram,
       my_control_1_immediate, my_control_1_rd_direction, my_control_1_write_en, my_ram_control_1_read_mem,
       my_ram_control_1_write_mem, not_1_out, not_2_out;
  wire [2:0] demultiplexer_1_out0, demultiplexer_1_out1, multiplexer_5_out;
  wire [3:0] multiplexer_8_out, my_control_1_alu_opcode, my_control_1_mem_word,
       my_ram_control_1_alu_add_for_mem;
  wire [7:0] demultiplexer_2_out0, demultiplexer_2_out1, demultiplexer_3_out0, demultiplexer_3_out1,
       multiplexer_1_out, multiplexer_2_out, multiplexer_6_out, multiplexer_7_out, my_8bit_alu_1_main_output,
       my_8bit_alu_2_main_output, my_register_file_1_rega, my_register_file_1_regb, ram_1_dout, register_1_q,
       rom_1_data;
  wire [15:0] rom_1_data_2;

  Register #(.trigger("falling")) register_1 (
    .D(multiplexer_1_out), .en(1'b1), .clk(clock_tunnel), .Q(register_1_q));  // open: clr
  Clock clock_1 (.out(clock_tunnel));
  Multiplexer #(.width(8)) multiplexer_1 (
    .in0(my_8bit_alu_1_main_output), .in1(multiplexer_2_out), .out(multiplexer_1_out), .sel(Jump));
  My_8Bit_ALU my_8bit_alu_1 (
    .A(8'h1), .B(register_1_q), .opcode(4'b0010), .main_output(my_8bit_alu_1_main_output),
    .is_zero(my_8bit_alu_1_is_zero), .overflow(my_8bit_alu_1_overflow));
  ROM #(.dataWidth(24)) rom_1 (.addr(register_1_q), .data({rom_1_data, rom_1_data_2}));
  LED led_1 (.in(my_8bit_alu_1_overflow));
  LED led_2 (.in(my_8bit_alu_1_is_zero));
  Multiplexer #(.width(8)) multiplexer_2 (
    .in0(my_8bit_alu_1_main_output), .in1(rom_1_data), .out(multiplexer_2_out), .sel(multiplexer_3_out));
  Multiplexer multiplexer_3 (.in0(my_8bit_alu_2_is_zero), .in1(not_1_out), .out(multiplexer_3_out), .sel(BNE));
  not not_1 (not_1_out, my_8bit_alu_2_is_zero);
  Demultiplexer #(.width(3)) demultiplexer_1 (
    .out0(demultiplexer_1_out0), .out1(demultiplexer_1_out1), .in(rom_1_data_2[9:7]), .sel(multiplexer_4_out));
  Multiplexer multiplexer_4 (
    .in0(my_control_1_go_to_ram), .in1(not_2_out), .out(multiplexer_4_out), .sel(my_control_1_rd_direction));
  not not_2 (not_2_out, my_control_1_go_to_ram);
  Multiplexer #(.width(3)) multiplexer_5 (
    .in0(rom_1_data_2[15:13]), .in1(demultiplexer_1_out1), .out(multiplexer_5_out),
    .sel(my_control_1_go_to_ram));
  Multiplexer #(.width(8)) multiplexer_6 (
    .in0(demultiplexer_3_out0), .in1(ram_1_dout), .out(multiplexer_6_out), .sel(my_control_1_go_to_ram));
  My_Register_File my_register_file_1 (
    .Clock(clock_tunnel), .write_en(my_control_1_write_en), .reg_ra_sel(rom_1_data_2[12:10]),
    .reg_rb_sel(multiplexer_5_out), .reg_w_sel(demultiplexer_1_out0), .Data(multiplexer_6_out),
    .regA(my_register_file_1_rega), .regB(my_register_file_1_regb));
  My_Control my_control_1 (
    .in_1(rom_1_data_2[6:0]), .rd_direction(my_control_1_rd_direction), .go_to_ram(my_control_1_go_to_ram),
    .ALU_opcode(my_control_1_alu_opcode), .Mem_word(my_control_1_mem_word),
    .Immediate(my_control_1_immediate), .write_en(my_control_1_write_en), .J(Jump), .BNE(BNE));
  Demultiplexer #(.width(8)) demultiplexer_2 (
    .out0(demultiplexer_2_out0), .out1(demultiplexer_2_out1), .in(my_register_file_1_regb),
    .sel(my_control_1_go_to_ram));
  Demultiplexer #(.width(8)) demultiplexer_3 (
    .out0(demultiplexer_3_out0), .out1(demultiplexer_3_out1), .in(my_8bit_alu_2_main_output),
    .sel(my_control_1_go_to_ram));
  Multiplexer #(.width(8)) multiplexer_7 (
    .in0(demultiplexer_2_out0), .in1(rom_1_data), .out(multiplexer_7_out), .sel(my_control_1_immediate));
  Multiplexer #(.width(4)) multiplexer_8 (
    .in0(my_control_1_alu_opcode), .in1(my_ram_control_1_alu_add_for_mem), .out(multiplexer_8_out),
    .sel(my_control_1_go_to_ram));
  My_8Bit_ALU my_8bit_alu_2 (
    .A(my_register_file_1_rega), .B(multiplexer_7_out), .opcode(multiplexer_8_out),
    .main_output(my_8bit_alu_2_main_output), .is_zero(my_8bit_alu_2_is_zero),
    .overflow(my_8bit_alu_2_overflow));
  LED led_3 (.in(my_8bit_alu_2_overflow));
  My_RAM_Control my_ram_control_1 (
    .in_1(my_control_1_mem_word), .ALU_add_for_mem(my_ram_control_1_alu_add_for_mem),
    .write_mem(my_ram_control_1_write_mem), .read_mem(my_ram_control_1_read_mem));
  LED led_4 (.in(my_8bit_alu_2_is_zero));
  RAM #(.asyncread("true"), .trigger("falling")) ram_1 (
    .addr(demultiplexer_3_out1), .we(my_ram_control_1_write_mem), .oe(my_ram_control_1_read_mem),
    .clk(clock_tunnel), .din(demultiplexer_2_out1), .dout(ram_1_dout));

  // Notes on the sheet:
  //   contents of rom_1 (hex, n*v repeats v):
  //   0 308a2 20d22 4592 2a16 4690 4711 6b97 699c 9fe a7a c6908 da80b 10008
endmodule

module My_Control (
  input  [6:0] in_1,
  output rd_direction,
  output go_to_ram,
  output [3:0] ALU_opcode,
  output [3:0] Mem_word,
  output Immediate,
  output write_en,
  output J,
  output BNE
);

  wire and_2_out, and_3_out, and_4_out, and_5_out, and_6_out, and_9_out, not_1_out, not_2_out, not_3_out,
       not_4_out, not_5_out, not_6_out, not_7_out, not_8_out, not_9_out, not_10_out, not_11_out;

  not not_1 (not_1_out, in_1[2]);
  and and_1 (rd_direction, in_1[3], not_1_out, in_1[1], not_2_out);
  not not_2 (not_2_out, in_1[0]);
  not not_3 (not_3_out, in_1[4]);
  not not_4 (not_4_out, in_1[0]);
  not not_5 (not_5_out, in_1[1]);
  not not_6 (not_6_out, in_1[2]);
  not not_7 (not_7_out, in_1[1]);
  not not_8 (not_8_out, in_1[2]);
  Demultiplexer #(.width(4)) demultiplexer_1 (.out0(ALU_opcode), .out1(Mem_word), .in(in_1[3:0]), .sel(in_1[6]));
  and and_2 (and_2_out, not_3_out, in_1[5]);
  and and_3 (and_3_out, in_1[4], in_1[5]);
  and and_4 (and_4_out, not_3_out, in_1[5]);
  and and_5 (and_5_out, in_1[4], not_9_out);
  not not_9 (not_9_out, in_1[5]);
  not not_10 (not_10_out, in_1[0]);
  and and_6 (and_6_out, not_10_out, in_1[1], not_11_out, in_1[3]);
  not not_11 (not_11_out, in_1[2]);
  and and_7 (J, not_4_out, not_5_out, not_6_out, in_1[3]);
  and and_8 (BNE, in_1[0], not_7_out, not_8_out, in_1[3]);
  and and_9 (and_9_out, and_3_out, in_1[6]);
  or or_1 (Immediate, and_2_out, and_9_out);
  or or_2 (write_en, and_4_out, and_6_out, and_5_out);

  assign go_to_ram = in_1[6];
endmodule

module My_RAM_Control (
  input  [3:0] in_1,
  output write_mem,
  output read_mem,
  output [3:0] ALU_add_for_mem
);

  wire and_1_out, and_2_out, and_3_out, and_4_out, not_1_out, not_2_out, not_3_out;
  wire [3:0] demultiplexer_1_out0, demultiplexer_1_out1;
  wire [3:2] not_5_out;
  wire [3:3] not_4_out;

  not not_1 (not_1_out, in_1[0]);
  not not_2 (not_2_out, in_1[0]);
  not not_3 (not_3_out, in_1[2]);
  Demultiplexer #(.width(4)) demultiplexer_1 (
    .out0(demultiplexer_1_out0), .out1(demultiplexer_1_out1), .in(in_1), .sel(in_1[2]));
  and and_1 (and_1_out, not_1_out, in_1[1]);
  and and_2 (and_2_out, in_1[2], in_1[3]);
  and and_3 (and_3_out, not_2_out, in_1[1]);
  and and_4 (and_4_out, not_3_out, in_1[3]);
  and and_5 (write_mem, and_1_out, and_2_out);
  and and_6 (read_mem, and_3_out, and_4_out);
  not not_4 (not_4_out[3], demultiplexer_1_out0[3]);
  not not_5 (not_5_out[2], demultiplexer_1_out1[2]);
  not not_6 (not_5_out[3], demultiplexer_1_out1[3]);
  Multiplexer #(.width(4)) multiplexer_1 (
    .in0({not_4_out[3], demultiplexer_1_out0[2:0]}), .in1({not_5_out, demultiplexer_1_out1[1:0]}),
    .out(ALU_add_for_mem), .sel(in_1[2]));
endmodule
